# Fritzing sketch Foosball (saved by Fritzing 0.8.7b)

parts:
  PWM1 = PCA9685 16x12-bit PWM Breakout
  PWM2 = PCA9685 16x12-bit PWM Breakout
  Onderdeel1 = Arduino Uno (Rev3)
  LED1 = LEDs [package=led10mm]
  LED2 = LED - 3mm [color="Red (633nm)" package="3 mm [THT]"]
  R3 = Resistor [tolerance=±5% resistance=330 package="1206 [SMD]"]
  R4 = Resistor [tolerance=±5% resistance=330 package="1206 [SMD]"]
  R5 = Resistor [tolerance=±5% resistance=330 package="1206 [SMD]"]
  R6 = Resistor [tolerance=±5% resistance=330 package="1206 [SMD]"]
  LED3 = LED - 3mm [color="Red (633nm)" package="3 mm [THT]"]
  LED4 = LED - 3mm [color="Red (633nm)" package="3 mm [THT]"]
  LED6 = LED - 3mm [color="Red (633nm)" package="3 mm [THT]"]
  U2 = Voltage Regulator [package=to220-adj]
  C1 = Ceramic Capacitor [capacitance=100nF package="200 mil [THT, multilayer]"]
  R7 = Resistor [tolerance=±0.5% resistance=300 package=THT]
  R8 = Resistor [tolerance=±0.5% resistance=240 package=THT]
  C2 = Electrolytic Capacitor [capacitance=1µF package="100 mil [THT, electrolytic]"]
  S1 = Round Pushbutton
  S2 = Round Pushbutton
  S3 = Round Pushbutton
  S4 = Round Pushbutton
  S5 = Round Pushbutton
  LED7 = LEDs [package=led10mm]
  U3 = Voltage Regulator [package=to220-adj]
  C3 = Ceramic Capacitor [capacitance=100nF package="200 mil [THT, multilayer]"]
  R9 = Resistor [tolerance=±0.5% resistance=300 package=THT]
  R10 = Resistor [tolerance=±0.5% resistance=240 package=THT]
  C4 = Electrolytic Capacitor [capacitance=1µF package="100 mil [THT, electrolytic]"]
  Q1 = LTR-301 [part_number=BPW40 package=ltr-301]
  R11 = Resistor [tolerance=±0.5% resistance=10k package=THT]
  R12 = Resistor [tolerance=±0.5% resistance=10k package=THT]
  Q2 = LTR-301 [part_number=BPW40 package=ltr-301]

nets:
  N1: PWM1.no_name_yet#0, LED6.anode
  N2: PWM1.no_name_yet#1, LED3.anode
  N3: PWM1.no_name_yet#2, LED2.anode
  N4: PWM1.no_name_yet#3, LED4.anode
  N5: PWM1.no_name_yet#501, PWM1.no_name_yet#502, PWM1.no_name_yet#601, PWM1.no_name_yet#602, PWM1.no_name_yet#701, PWM1.no_name_yet#1000, PWM1.no_name_yet#1001, PWM1.no_name_yet#1002, PWM1.no_name_yet#1003, PWM2.no_name_yet#501, PWM2.no_name_yet#502, PWM2.no_name_yet#701, Onderdeel1.GND
  N6: PWM1.no_name_yet#503, PWM1.no_name_yet#603, PWM2.no_name_yet#503, Onderdeel1.A5/SCL
  N7: PWM1.no_name_yet#504, PWM1.no_name_yet#604, PWM2.no_name_yet#504, Onderdeel1.A4/SDA
  N8: PWM1.no_name_yet#505, PWM1.no_name_yet#506, PWM1.no_name_yet#605, PWM1.no_name_yet#606, PWM1.no_name_yet#706, PWM2.no_name_yet#505, PWM2.no_name_yet#506, PWM2.no_name_yet#706, Onderdeel1.5V
  N9: Onderdeel1.A0, R11.Pin_1, Q2.E
  N10: Onderdeel1.D2, S4.leg1
  N11: Onderdeel1.D3_PWM, S3.leg1
  N12: Onderdeel1.D4, S5.leg0, S5.leg1
  N13: Onderdeel1.D5_PWM, S2.leg1
  N14: Onderdeel1.D6_PWM, S1.leg1
  N15: LED1.A, U2.OUT, R8.Pin_0, C2.+
  N16: LED1.C, C1.0, R7.Pin_1, C2.-
  N17: LED2.cathode, R5.Pin_1
  N18: R3.Pin_1, LED6.cathode
  N19: R4.Pin_1, LED4.cathode
  N20: R6.Pin_1, LED3.cathode
  N21: U2.ADJ, R7.Pin_0, R8.Pin_1
  N22: U2.IN, C1.1
  N23: S1.leg0, S4.leg0
  N24: LED7.A, U3.OUT, R10.Pin_0, C4.+
  N25: LED7.C, C3.0, R9.Pin_1, C4.-
  N26: U3.ADJ, R9.Pin_0, R10.Pin_1
  N27: U3.IN, C3.1
  N28: Q1.E, R12.Pin_1
